# Fritzing sketch pico_paa5160e1_schematic (saved by Fritzing 0.9.6b)
breadboards: 1

parts:
  Mod1 = Raspberry Pi Pico
  IC1 = DIP - 6 pins [package="DIP (Dual Inline) [THT]"]

nets:
  N1: Mod1.pin_3, Mod1.pin_8, Mod1.pin_13, Mod1.pin_18, Mod1.pin_23, Mod1.pin_28, Mod1.pin_33, Mod1.pin_38, IC1.GND
  N2: Mod1.pin_6, IC1.SDA
  N3: Mod1.pin_7, IC1.SCL
  N4: Mod1.pin_36, IC1.3V3

custom parts:
  Raspberry Pi Pico: Raspberry Pi Pico. Based around the RP2040 microcontroller the Pico is a low cost microcontroller device bringing Raspberry Pi quality, cost, and easy of use to the microcontroller space. Jan 2021, Split part in to two versions: tht (this one) and SMD. This one will drill holes for a .1 in header in pcb to allow plugging in the module as well as providing pads to solder the module to the top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
  DIP - 6 pins: A DIP stand-in part for whatever IC you want. With 6 pins on a 300mil dual inline package (DIP) footprint.
